# Fritzing sketch ReflowOven (saved by Fritzing 0.9.3b)

parts:
  Bauteil1 = Arduino Uno (Rev3)
  TFT_2_1 = TFT 2.4 [part_number="TFT 2.4"]  # not connected
  U1 = MAX6675 [package=so08]
  U3 = RELAY-SOLIDSTATE [package=relay-s108t02]
  F1 = FUSE [package=fuse_5mm]
  L1 = Inductor [package="1206 [SMD]"]
  L2 = Inductor [package="1206 [SMD]"]

nets:
  N1: Bauteil1.A5/SCL, U3.+
  N2: Bauteil1.D10_PWM/SS, U1.SCK
  N3: Bauteil1.D11_PWM/MOSI, U1.CS
  N4: Bauteil1.D12/MISO, U1.MISO
  5V: Bauteil1.5V, U1.VDD
  GND: Bauteil1.GND, U1.VSS, U3.-
  N5: U3.T1, L2.pin_1
  N6: F1.2, L1.pin_0
  N7: L1.pin_1, L2.pin_0
